// Logisim project ExecuteBootleg.circ as structural Verilog
module main (
  input  icode,
  input  ifun,
  input  ValA,
  input  ValB,
  input  ValC,
  output ValE,
  output PCUpdate
);
endmodule

module ALU (
  input  [63:0] A,
  input  [63:0] B,
  input  [1:0] notFun,
  output [63:0] valE
);

  wire [63:0] adder_1_out, and_1_out, subtractor_1_out, xor_1_out;

  Adder #(.width(64)) adder_1 (.a(A), .b(B), .out(adder_1_out));  // open: cin, cout
  Subtractor #(.width(64)) subtractor_1 (.a(A), .b(B), .out(subtractor_1_out));  // open: bin, bout
  assign and_1_out = A & B;  // AND_Gate and_1, 64 bits wide
  assign xor_1_out = A ^ B;  // XOR_Gate xor_1, 64 bits wide
  Multiplexer #(.select(2), .width(64)) multiplexer_1 (
    .in0(adder_1_out), .in1(subtractor_1_out), .in2(and_1_out), .in3(xor_1_out), .out(valE), .sel(notFun));
endmodule

module CTRLogic (
  input  icode,
  input  valA,
  input  valB,
  input  valC,
  output A,
  output B
);
endmodule

module ALUA (
  input  icode,
  input  valA,
  input  valC,
  output A
);
endmodule

module ALUB (
  input  icode,
  input  valB,
  output B
);
endmodule

module ALUfun (
  input  icode,
  input  ifun,
  output noCodeNoFun
);
endmodule
