// Logisim project Lab6.circ as structural Verilog
module main (
);

  wire clock_1_out;

  ROM rom_1 ();  // open: addr, data
  Clock clock_1 (.out(clock_1_out));
  RAM ram_1 ();  // open: addr, we, oe, clk, din, dout
endmodule
